# Fritzing sketch Schaltung (saved by Fritzing 0.9.6b)

parts:
  R1 = Resistor [tolerance=±5% resistance=1k package="2010 [SMD]"]
  U1 = ESP8266 NodeMCU LoLin module
  S0_interface_power_meter = Reed switch [package=THT]

nets:
  N1: R1.Pin_0, U1.D2, U1.D3, S0_interface_power_meter.pin_1
  N2: R1.Pin_1, U1.3V3
  N3: U1.GND, S0_interface_power_meter.pin_2

notes:
  S0+
  S0-

custom parts:
  ESP8266 NodeMCU LoLin module: ESP8266 based NodeMCU
