# Fritzing sketch Schaltung (saved by Fritzing 0.9.6b)

parts:
  S0_interface_power_meter = Reed switch [package=THT]
  U1 = ESP8266 NodeMCU LoLin module
  R1 = Resistor [tolerance=±5% resistance=1k package="2010 [SMD]"]

nets:
  N1: S0_interface_power_meter.pin_1, U1.D2, U1.D3, R1.Pin_0
  N2: S0_interface_power_meter.pin_2, U1.GND
  N3: U1.3V3, R1.Pin_1

notes:
  S0+
  S0-

custom parts:
  ESP8266 NodeMCU LoLin module: ESP8266 based NodeMCU
